# Fritzing sketch Connection (saved by Fritzing 0.9.3b)

parts:
  GY2 = MPU-6050 Board GY-521 [form="♀ (female)" package=THT]
  HC-SR04_Sensor_1 = HC-SR04 Ultrasonic Distance Sensor
  YL-83_-_Control_Board2 = YL-83 Rain Sensor - Control Board
  YL-83_-_Detection_Board2 = YL-83 Rain Sensor - Detection Board
  U6 = NodeMCU V1.0
  J2 = Infrared Proximity Sensor
  Part1 = Passive Buzzer
  DFRobot-DFPlayer-Mini2 = DFRobot DFPlayer Mini [part_number=DFR0299]
  SPKR2 = Loudspeaker  # not connected

nets:
  VCC: GY2.pin1, HC-SR04_Sensor_1.VCC, U6.3V3, J2.Vcc, Part1.S, DFRobot-DFPlayer-Mini2.VCC
  GND: GY2.pin2, HC-SR04_Sensor_1.GND, YL-83_-_Control_Board2.GND, U6.GND, J2.GND, Part1.GND, DFRobot-DFPlayer-Mini2.GND-1, DFRobot-DFPlayer-Mini2.GND-2
  N1: GY2.pin3, U6.D1
  N2: GY2.pin4, U6.D2
  N3: HC-SR04_Sensor_1.TRIG, U6.D5
  N4: HC-SR04_Sensor_1.ECHO, U6.D6
  VCC_2: YL-83_-_Control_Board2.VCC, U6.Vin
  N5: YL-83_-_Control_Board2.AO, U6.A0, J2.Vout
  N6: YL-83_-_Control_Board2.POS, YL-83_-_Detection_Board2.POS
  N7: YL-83_-_Control_Board2.NEG, YL-83_-_Detection_Board2.NEG
  N8: U6.D0, Part1.NC
  N9: U6.D7, DFRobot-DFPlayer-Mini2.RX
  N10: U6.D8, DFRobot-DFPlayer-Mini2.TX

custom parts:
  MPU-6050 Board GY-521: Acelerometro y Giroscopio MPU-6050 Board GY-521
  YL-83 Rain Sensor - Control Board: The YL-83 is a rain sensor that has more resistance when dry and less resistance when wet. The module runs at 5V.
  YL-83 Rain Sensor - Detection Board: The YL-83 is a rain sensor that has more resistance when dry and less resistance when wet. The module runs at 5V.
  NodeMCU V1.0: ESP8266 based NodeMCU
